// Logisim project clock.circ as structural Verilog: 4 circuits, main circuit main
module main (
  input  Minutes,
  input  Hours
);

  wire clock_1_out, j_k_ff_1_q, j_k_ff_1_qn, j_k_ff_2_qn, l_74ls247_478a221e_1_a, l_74ls247_478a221e_1_b,
       l_74ls247_478a221e_1_c, l_74ls247_478a221e_1_d, l_74ls247_478a221e_1_e, l_74ls247_478a221e_1_f,
       l_74ls247_478a221e_1_g, l_74ls247_478a221e_2_a, l_74ls247_478a221e_2_b, l_74ls247_478a221e_2_c,
       l_74ls247_478a221e_2_d, l_74ls247_478a221e_2_e, l_74ls247_478a221e_2_f, l_74ls247_478a221e_2_g,
       l_74ls247_478a221e_3_a, l_74ls247_478a221e_3_b, l_74ls247_478a221e_3_c, l_74ls247_478a221e_3_d,
       l_74ls247_478a221e_3_e, l_74ls247_478a221e_3_f, l_74ls247_478a221e_3_g, l_74ls247_478a221e_4_a,
       l_74ls247_478a221e_4_b, l_74ls247_478a221e_4_c, l_74ls247_478a221e_4_d, l_74ls247_478a221e_4_e,
       l_74ls247_478a221e_4_f, l_74ls247_478a221e_4_g, l_74ls247_478a221e_5_a, l_74ls247_478a221e_5_b,
       l_74ls247_478a221e_5_c, l_74ls247_478a221e_5_d, l_74ls247_478a221e_5_e, l_74ls247_478a221e_5_f,
       l_74ls247_478a221e_5_g, multiplexer_1_out, multiplexer_2_out, nand_1_out, nand_2_out, nand_3_out,
       nand_4_out;
  wire [2:0] l_74ls90_a0c69b36_2_qa, l_74ls90_a0c69b36_4_qa;
  wire [3:0] l_74ls90_a0c69b36_1_qa, l_74ls90_a0c69b36_3_qa, l_74ls163_73082773_1_qa;

  L_74LS247_478a221e l_74ls247_478a221e_1 (
    .nRBI(1'b1), .in_3(l_74ls90_a0c69b36_4_qa[0]), .VCC(1'b1), .in_4(l_74ls90_a0c69b36_4_qa[1]),
    .in_5(l_74ls90_a0c69b36_4_qa[2]), .in_6(1'b0), .nLT(1'b1), .GND(1'b0), .g(l_74ls247_478a221e_1_g),
    .a(l_74ls247_478a221e_1_a), .b(l_74ls247_478a221e_1_b), .c(l_74ls247_478a221e_1_c),
    .d(l_74ls247_478a221e_1_d), .e(l_74ls247_478a221e_1_e), .f(l_74ls247_478a221e_1_f));  // open: nBI_nRBO_319084ec
  L_74LS247_478a221e l_74ls247_478a221e_2 (
    .nRBI(1'b1), .in_3(l_74ls163_73082773_1_qa[0]), .VCC(1'b1), .in_4(l_74ls163_73082773_1_qa[1]),
    .in_5(l_74ls163_73082773_1_qa[2]), .in_6(l_74ls163_73082773_1_qa[3]), .nLT(1'b1), .GND(1'b0),
    .g(l_74ls247_478a221e_2_g), .a(l_74ls247_478a221e_2_a), .b(l_74ls247_478a221e_2_b),
    .c(l_74ls247_478a221e_2_c), .d(l_74ls247_478a221e_2_d), .e(l_74ls247_478a221e_2_e),
    .f(l_74ls247_478a221e_2_f));  // open: nBI_nRBO_319084ec
  LED #(.active("false")) PM (.in(j_k_ff_2_qn));
  _7_Segment_Display #(.active("false")) u_7_segment_display_1 (
    .g(1'b1), .f(1'b1), .a(1'b1), .b(j_k_ff_1_qn), .e(1'b1), .d(1'b1), .c(j_k_ff_1_qn), .dp(1'b1));
  Clock clock_1 (.out(clock_1_out));
  _7_Segment_Display #(.active("false")) u_7_segment_display_2 (
    .g(l_74ls247_478a221e_2_g), .f(l_74ls247_478a221e_2_f), .a(l_74ls247_478a221e_2_a),
    .b(l_74ls247_478a221e_2_b), .e(l_74ls247_478a221e_2_e), .d(l_74ls247_478a221e_2_d),
    .c(l_74ls247_478a221e_2_c), .dp(1'b1));
  LED led_1 (.in(1'b1));
  LED led_2 (.in(1'b1));
  L_74LS90_a0c69b36 l_74ls90_a0c69b36_1 (
    .VCC(1'b1), .R9_1_9d93a587(1'b0), .R9_2_00c0d31d(1'b0), .nCKA(clock_1_out),
    .nCKB(l_74ls90_a0c69b36_1_qa[0]), .R0_1_6208891d(1'b0), .R0_2_e012303e(1'b0), .GND(1'b0),
    .QA(l_74ls90_a0c69b36_1_qa[0]), .QB(l_74ls90_a0c69b36_1_qa[1]), .QC(l_74ls90_a0c69b36_1_qa[2]),
    .QD(l_74ls90_a0c69b36_1_qa[3]));  // open: out_9, NC
  _7_Segment_Display #(.active("false")) u_7_segment_display_3 (
    .g(l_74ls247_478a221e_1_g), .f(l_74ls247_478a221e_1_f), .a(l_74ls247_478a221e_1_a),
    .b(l_74ls247_478a221e_1_b), .e(l_74ls247_478a221e_1_e), .d(l_74ls247_478a221e_1_d),
    .c(l_74ls247_478a221e_1_c), .dp(1'b1));
  _7_Segment_Display #(.active("false")) u_7_segment_display_4 (
    .g(l_74ls247_478a221e_5_g), .f(l_74ls247_478a221e_5_f), .a(l_74ls247_478a221e_5_a),
    .b(l_74ls247_478a221e_5_b), .e(l_74ls247_478a221e_5_e), .d(l_74ls247_478a221e_5_d),
    .c(l_74ls247_478a221e_5_c), .dp(1'b1));
  LED led_3 (.in(1'b1));
  _7_Segment_Display #(.active("false")) u_7_segment_display_5 (
    .g(l_74ls247_478a221e_4_g), .f(l_74ls247_478a221e_4_f), .a(l_74ls247_478a221e_4_a),
    .b(l_74ls247_478a221e_4_b), .e(l_74ls247_478a221e_4_e), .d(l_74ls247_478a221e_4_d),
    .c(l_74ls247_478a221e_4_c), .dp(1'b1));
  LED led_4 (.in(1'b1));
  L_74LS90_a0c69b36 l_74ls90_a0c69b36_2 (
    .VCC(1'b1), .R9_1_9d93a587(1'b0), .R9_2_00c0d31d(1'b0), .nCKA(l_74ls90_a0c69b36_1_qa[3]),
    .nCKB(l_74ls90_a0c69b36_2_qa[0]), .R0_1_6208891d(l_74ls90_a0c69b36_2_qa[1]),
    .R0_2_e012303e(l_74ls90_a0c69b36_2_qa[2]), .GND(1'b0), .QA(l_74ls90_a0c69b36_2_qa[0]),
    .QB(l_74ls90_a0c69b36_2_qa[1]), .QC(l_74ls90_a0c69b36_2_qa[2]));  // open: out_9, NC, QD
  _7_Segment_Display #(.active("false")) u_7_segment_display_6 (
    .g(l_74ls247_478a221e_3_g), .f(l_74ls247_478a221e_3_f), .a(l_74ls247_478a221e_3_a),
    .b(l_74ls247_478a221e_3_b), .e(l_74ls247_478a221e_3_e), .d(l_74ls247_478a221e_3_d),
    .c(l_74ls247_478a221e_3_c), .dp(1'b1));
  Multiplexer multiplexer_1 (
    .in0(l_74ls90_a0c69b36_2_qa[2]), .in1(clock_1_out), .out(multiplexer_1_out), .sel(Minutes));
  L_74LS247_478a221e l_74ls247_478a221e_3 (
    .nRBI(1'b1), .in_3(l_74ls90_a0c69b36_1_qa[0]), .VCC(1'b1), .in_4(l_74ls90_a0c69b36_1_qa[1]),
    .in_5(l_74ls90_a0c69b36_1_qa[2]), .in_6(l_74ls90_a0c69b36_1_qa[3]), .nLT(1'b1), .GND(1'b0),
    .g(l_74ls247_478a221e_3_g), .a(l_74ls247_478a221e_3_a), .b(l_74ls247_478a221e_3_b),
    .c(l_74ls247_478a221e_3_c), .d(l_74ls247_478a221e_3_d), .e(l_74ls247_478a221e_3_e),
    .f(l_74ls247_478a221e_3_f));  // open: nBI_nRBO_319084ec
  L_74LS90_a0c69b36 l_74ls90_a0c69b36_3 (
    .VCC(1'b1), .R9_1_9d93a587(1'b0), .R9_2_00c0d31d(1'b0), .nCKA(multiplexer_1_out),
    .nCKB(l_74ls90_a0c69b36_3_qa[0]), .R0_1_6208891d(1'b0), .R0_2_e012303e(1'b0), .GND(1'b0),
    .QA(l_74ls90_a0c69b36_3_qa[0]), .QB(l_74ls90_a0c69b36_3_qa[1]), .QC(l_74ls90_a0c69b36_3_qa[2]),
    .QD(l_74ls90_a0c69b36_3_qa[3]));  // open: out_9, NC
  L_74LS90_a0c69b36 l_74ls90_a0c69b36_4 (
    .VCC(1'b1), .R9_1_9d93a587(1'b0), .R9_2_00c0d31d(1'b0), .nCKA(l_74ls90_a0c69b36_3_qa[3]),
    .nCKB(l_74ls90_a0c69b36_4_qa[0]), .R0_1_6208891d(l_74ls90_a0c69b36_4_qa[1]),
    .R0_2_e012303e(l_74ls90_a0c69b36_4_qa[2]), .GND(1'b0), .QA(l_74ls90_a0c69b36_4_qa[0]),
    .QB(l_74ls90_a0c69b36_4_qa[1]), .QC(l_74ls90_a0c69b36_4_qa[2]));  // open: out_9, NC, QD
  L_74LS247_478a221e l_74ls247_478a221e_4 (
    .nRBI(1'b1), .in_3(l_74ls90_a0c69b36_2_qa[0]), .VCC(1'b1), .in_4(l_74ls90_a0c69b36_2_qa[1]),
    .in_5(l_74ls90_a0c69b36_2_qa[2]), .in_6(1'b0), .nLT(1'b1), .GND(1'b0), .g(l_74ls247_478a221e_4_g),
    .a(l_74ls247_478a221e_4_a), .b(l_74ls247_478a221e_4_b), .c(l_74ls247_478a221e_4_c),
    .d(l_74ls247_478a221e_4_d), .e(l_74ls247_478a221e_4_e), .f(l_74ls247_478a221e_4_f));  // open: nBI_nRBO_319084ec
  L_74LS247_478a221e l_74ls247_478a221e_5 (
    .nRBI(1'b1), .in_3(l_74ls90_a0c69b36_3_qa[0]), .VCC(1'b1), .in_4(l_74ls90_a0c69b36_3_qa[1]),
    .in_5(l_74ls90_a0c69b36_3_qa[2]), .in_6(l_74ls90_a0c69b36_3_qa[3]), .nLT(1'b1), .GND(1'b0),
    .g(l_74ls247_478a221e_5_g), .a(l_74ls247_478a221e_5_a), .b(l_74ls247_478a221e_5_b),
    .c(l_74ls247_478a221e_5_c), .d(l_74ls247_478a221e_5_d), .e(l_74ls247_478a221e_5_e),
    .f(l_74ls247_478a221e_5_f));  // open: nBI_nRBO_319084ec
  Multiplexer multiplexer_2 (.in0(l_74ls90_a0c69b36_4_qa[2]), .in1(clock_1_out), .out(multiplexer_2_out), .sel(Hours));
  L_74LS163_73082773 l_74ls163_73082773_1 (
    .nLOAD(nand_3_out), .A(1'b1), .B(1'b0), .CLK(nand_1_out), .C(1'b0), .D(1'b0), .nCLR(nand_2_out),
    .ENP(1'b1), .ENT(1'b1), .VCC(1'b1), .GND(1'b0), .QA(l_74ls163_73082773_1_qa[0]),
    .QB(l_74ls163_73082773_1_qa[1]), .QC(l_74ls163_73082773_1_qa[2]), .QD(l_74ls163_73082773_1_qa[3]));  // open: RCO
  nand nand_1 (nand_1_out, multiplexer_2_out, multiplexer_2_out);
  nand nand_2 (nand_2_out, l_74ls163_73082773_1_qa[0], l_74ls163_73082773_1_qa[3]);
  nand nand_3 (nand_3_out, l_74ls163_73082773_1_qa[1], j_k_ff_1_q);
  nand nand_4 (nand_4_out, nand_2_out, nand_3_out);
  J_K_Flip_Flop #(.trigger("falling")) j_k_ff_1 (
    .J(1'b1), .clk(nand_4_out), .K(1'b1), .Q(j_k_ff_1_q), .Qn(j_k_ff_1_qn));  // open: preset, reset
  J_K_Flip_Flop #(.trigger("falling")) j_k_ff_2 (
    .J(1'b1), .clk(nand_3_out), .K(1'b1), .Qn(j_k_ff_2_qn));  // open: Q, preset, reset

  // Notes on the sheet:
  //   1 - 1Hz oscillator
  //   4 - decade counters (7490)
  //   1 - binary counter (74163)
  //   4 - 2-input NAND gates (7400)
  //   2 - negedge JK-flip-flops (7473)
  //   6/4 - 7-seg displays
  //   5/3 - LEDs
  //   2 - SPDT push buttons
  //   5/3 - BCD to 7-seg decoders (74247)
  //   feedback loop
endmodule

module L_74LS247_478a221e (
  input  VCC,
  input  GND,
  input  in_3,
  input  in_4,
  input  in_5,
  input  in_6,
  input  nLT,
  input  nRBI,
  output a,
  output b,
  output c,
  output d,
  output e,
  output nBI_nRBO_319084ec,
  output f,
  output g
);

  wire and_1_out, and_2_out, and_3_out, and_4_out, and_5_out, and_6_out, and_7_out, and_8_out, and_9_out,
       and_10_out, and_11_out, and_12_out, and_13_out, and_14_out, and_15_out, and_16_out, and_17_out,
       buffer_1_out, nand_1_out, nand_2_out, nand_3_out, nand_4_out, nand_5_out, nand_6_out, nand_7_out,
       nor_1_out, nor_2_out, nor_3_out, nor_4_out, nor_5_out, nor_6_out, nor_7_out, not_1_out, not_2_out,
       not_3_out, not_4_out, not_5_out, not_6_out;

  nand nand_1 (nand_1_out, in_3, not_2_out);
  nand nand_2 (nand_2_out, in_4, not_2_out);
  nand nand_3 (nand_3_out, in_5, not_2_out);
  not not_1 (not_1_out, in_6);
  not not_2 (not_2_out, not_3_out);
  not not_3 (not_3_out, nLT);
  not not_4 (not_4_out, nRBI);
  nand nand_4 (nand_4_out, nand_1_out, not_5_out);
  nand nand_5 (nand_5_out, nand_2_out, not_5_out);
  nand nand_6 (nand_6_out, nand_3_out, not_5_out);
  nand nand_7 (nand_7_out, not_1_out, not_5_out);
  not not_5 (not_5_out, not_6_out);
  not not_6 (not_6_out, nBI_nRBO_319084ec);
  nand nand_8 (nBI_nRBO_319084ec, not_2_out, not_4_out, not_1_out, nand_3_out, nand_2_out, nand_1_out);
  and and_1 (and_1_out, nand_5_out, nand_7_out);
  and and_2 (and_2_out, nand_1_out, nand_2_out, nand_6_out);
  and and_3 (and_3_out, nand_4_out, nand_2_out, nand_3_out, not_1_out);
  and and_4 (and_4_out, nand_5_out, nand_7_out);
  and and_5 (and_5_out, nand_4_out, nand_2_out, nand_6_out);
  and and_6 (and_6_out, nand_1_out, nand_5_out, nand_6_out);
  and and_7 (and_7_out, nand_6_out, nand_7_out);
  and and_8 (and_8_out, nand_1_out, nand_5_out, nand_3_out);
  and and_9 (and_9_out, nand_4_out, nand_2_out, nand_3_out, not_1_out);
  and and_10 (and_10_out, nand_1_out, nand_2_out, nand_6_out);
  and and_11 (and_11_out, nand_4_out, nand_5_out, nand_6_out);
  buf buffer_1 (buffer_1_out, nand_4_out);
  and and_12 (and_12_out, nand_2_out, nand_6_out);
  and and_13 (and_13_out, nand_4_out, nand_5_out);
  and and_14 (and_14_out, nand_5_out, nand_3_out);
  and and_15 (and_15_out, nand_4_out, nand_3_out, not_1_out);
  and and_16 (and_16_out, nand_4_out, nand_5_out, nand_6_out);
  and and_17 (and_17_out, nand_2_out, nand_3_out, not_1_out, not_2_out);
  nor nor_1 (nor_1_out, and_1_out, and_2_out, and_3_out);
  nor nor_2 (nor_2_out, and_4_out, and_5_out, and_6_out);
  nor nor_3 (nor_3_out, and_7_out, and_8_out);
  nor nor_4 (nor_4_out, and_9_out, and_10_out, and_11_out);
  nor nor_5 (nor_5_out, buffer_1_out, and_12_out);
  nor nor_6 (nor_6_out, and_13_out, and_14_out, and_15_out);
  nor nor_7 (nor_7_out, and_16_out, and_17_out);
  not not_7 (a, nor_1_out);
  not not_8 (b, nor_2_out);
  not not_9 (c, nor_3_out);
  not not_10 (d, nor_4_out);
  not not_11 (e, nor_5_out);
  not not_12 (f, nor_6_out);
  not not_13 (g, nor_7_out);

  // Notes on the sheet:
  //   = AB'C'D' + A'B'C + BD
  //   = AB'C + A'BC + BD
  //   = A'BC' + CD
  //   = AB'C'D' + ABC + A'B'C
  //   = A + B'C
  //   = AC'D' + AB + BC'
  //   = ABC + B'C'D'
endmodule

module L_74LS90_a0c69b36 (
  input  VCC,
  input  GND,
  input  R9_1_9d93a587,
  input  R9_2_00c0d31d,
  input  nCKA,
  input  nCKB,
  input  R0_1_6208891d,
  input  R0_2_e012303e,
  output out_9,
  output NC,
  output QA,
  output QB,
  output QC,
  output QD
);

  wire and_1_out, nand_1_out, nand_2_out, not_1_out, not_2_out, not_3_out, not_4_out, not_5_out, not_6_out,
       not_7_out, not_8_out, or_1_out, or_2_out, s_r_ff_1_qn;

  nand nand_1 (nand_1_out, R9_1_9d93a587, R9_2_00c0d31d);
  nand nand_2 (nand_2_out, R0_1_6208891d, R0_2_e012303e);
  not not_1 (not_1_out, nCKA);
  not not_2 (not_2_out, nand_1_out);
  not not_3 (not_3_out, nCKB);
  not not_4 (not_4_out, QB);
  and and_1 (and_1_out, QC, QB);
  not not_5 (not_5_out, nCKB);
  not not_6 (not_6_out, nand_1_out);
  J_K_Flip_Flop j_k_ff_1 (
    .J(1'b1), .clk(not_1_out), .K(1'b1), .Q(QA), .preset(not_2_out), .reset(not_7_out));  // open: Qn
  not not_7 (not_7_out, nand_2_out);
  J_K_Flip_Flop j_k_ff_2 (.J(s_r_ff_1_qn), .clk(not_3_out), .K(1'b1), .Q(QB), .reset(or_1_out));  // open: Qn, preset
  or or_1 (or_1_out, ~nand_2_out, ~nand_1_out);  // OR_Gate
  J_K_Flip_Flop j_k_ff_3 (.J(1'b1), .clk(not_4_out), .K(1'b1), .Q(QC), .reset(or_2_out));  // open: Qn, preset
  or or_2 (or_2_out, ~nand_2_out, ~nand_1_out);  // OR_Gate
  S_R_Flip_Flop s_r_ff_1 (
    .S(and_1_out), .clk(not_5_out), .R(QD), .Q(QD), .Qn(s_r_ff_1_qn), .preset(not_6_out), .reset(not_8_out));
  not not_8 (not_8_out, nand_2_out);
endmodule

module L_74LS163_73082773 (
  input  VCC,
  input  GND,
  input  nLOAD,
  input  A,
  input  B,
  input  CLK,
  input  C,
  input  D,
  input  nCLR,
  input  ENP,
  input  ENT,
  output QA,
  output QB,
  output QC,
  output QD,
  output RCO
);

  wire and_1_out, and_2_out, and_3_out, and_4_out, and_5_out, and_6_out, and_7_out, and_8_out, and_9_out,
       and_10_out, and_11_out, and_12_out, nand_1_out, nand_2_out, nand_3_out, nand_4_out, nand_5_out,
       nand_6_out, nand_7_out, nand_8_out, not_1_out, not_2_out, not_3_out, or_1_out, or_2_out, or_3_out,
       or_4_out, or_5_out;

  not not_1 (not_1_out, nCLR);
  not not_2 (not_2_out, not_1_out);
  and and_1 (and_1_out, ENP, ENT);
  or or_1 (or_1_out, ~nLOAD, ~not_2_out);  // OR_Gate
  and and_2 (and_2_out, QA, and_1_out);
  not not_3 (not_3_out, CLK);
  and and_3 (and_3_out, QB, QA, and_1_out);
  and and_4 (and_4_out, QC, QB, QA, and_1_out);
  nand nand_1 (nand_1_out, or_1_out, nand_2_out);
  or or_2 (or_2_out, and_1_out, or_1_out);
  nand nand_2 (nand_2_out, A, not_2_out, or_1_out);
  nand nand_3 (nand_3_out, or_1_out, nand_4_out);
  or or_3 (or_3_out, and_2_out, or_1_out);
  nand nand_4 (nand_4_out, B, not_2_out, or_1_out);
  nand nand_5 (nand_5_out, or_1_out, nand_6_out);
  or or_4 (or_4_out, and_3_out, or_1_out);
  nand nand_6 (nand_6_out, C, not_2_out, or_1_out);
  nand nand_7 (nand_7_out, or_1_out, nand_8_out);
  or or_5 (or_5_out, and_4_out, or_1_out);
  nand nand_8 (nand_8_out, D, or_1_out, not_2_out);
  and and_5 (and_5_out, nand_1_out, or_2_out);
  and and_6 (and_6_out, or_2_out, nand_2_out);
  and and_7 (and_7_out, nand_3_out, or_3_out);
  and and_8 (and_8_out, or_3_out, nand_4_out);
  and and_9 (and_9_out, nand_5_out, or_4_out);
  and and_10 (and_10_out, or_4_out, nand_6_out);
  and and_11 (and_11_out, nand_7_out, or_5_out);
  and and_12 (and_12_out, or_5_out, nand_8_out);
  J_K_Flip_Flop #(.trigger("falling")) j_k_ff_1 (
    .J(and_5_out), .clk(not_3_out), .K(and_6_out), .Q(QA));  // open: Qn, preset, reset
  J_K_Flip_Flop #(.trigger("falling")) j_k_ff_2 (
    .J(and_7_out), .clk(not_3_out), .K(and_8_out), .Q(QB));  // open: Qn, preset, reset
  J_K_Flip_Flop #(.trigger("falling")) j_k_ff_3 (
    .J(and_9_out), .clk(not_3_out), .K(and_10_out), .Q(QC));  // open: Qn, preset, reset
  J_K_Flip_Flop #(.trigger("falling")) j_k_ff_4 (
    .J(and_11_out), .clk(not_3_out), .K(and_12_out), .Q(QD));  // open: Qn, preset, reset
  and and_13 (RCO, QD, QC, QB, QA, ENT);
endmodule
