// Logisim project clock.circ as structural Verilog: 4 circuits, main circuit main
module main (
  input  Minutes,
  input  Hours
);

  wire clock_1_out, j_k_ff_1_q, j_k_ff_1_qn, j_k_ff_2_qn, multiplexer_1_out, multiplexer_2_out,
       n74ls247_1_a_2, n74ls247_1_b_2, n74ls247_1_c_2, n74ls247_1_d_2, n74ls247_1_e, n74ls247_1_f,
       n74ls247_1_g, n74ls247_2_a_2, n74ls247_2_b_2, n74ls247_2_c_2, n74ls247_2_d_2, n74ls247_2_e,
       n74ls247_2_f, n74ls247_2_g, n74ls247_3_a_2, n74ls247_3_b_2, n74ls247_3_c_2, n74ls247_3_d_2,
       n74ls247_3_e, n74ls247_3_f, n74ls247_3_g, n74ls247_4_a_2, n74ls247_4_b_2, n74ls247_4_c_2,
       n74ls247_4_d_2, n74ls247_4_e, n74ls247_4_f, n74ls247_4_g, n74ls247_5_a_2, n74ls247_5_b_2,
       n74ls247_5_c_2, n74ls247_5_d_2, n74ls247_5_e, n74ls247_5_f, n74ls247_5_g, nand_1_out, nand_2_out,
       nand_3_out, nand_4_out;
  wire [2:0] n74ls90_2_qa, n74ls90_4_qa;
  wire [3:0] n74ls90_1_qa, n74ls90_3_qa, n74ls163_1_qa;

  _74LS247 u_74ls247_1 (
    .A(n74ls90_4_qa[0]), .B(n74ls90_4_qa[1]), .C(n74ls90_4_qa[2]), .D(1'b0), .nLT(1'b1), .nRBI(1'b1),
    .a_2(n74ls247_1_a_2), .b_2(n74ls247_1_b_2), .c_2(n74ls247_1_c_2), .d_2(n74ls247_1_d_2), .e(n74ls247_1_e),
    .f(n74ls247_1_f), .g(n74ls247_1_g), .VCC(1'b1), .GND(1'b0));  // open: nBI_nRBO
  _74LS247 u_74ls247_2 (
    .A(n74ls163_1_qa[0]), .B(n74ls163_1_qa[1]), .C(n74ls163_1_qa[2]), .D(n74ls163_1_qa[3]), .nLT(1'b1),
    .nRBI(1'b1), .a_2(n74ls247_2_a_2), .b_2(n74ls247_2_b_2), .c_2(n74ls247_2_c_2), .d_2(n74ls247_2_d_2),
    .e(n74ls247_2_e), .f(n74ls247_2_f), .g(n74ls247_2_g), .VCC(1'b1), .GND(1'b0));  // open: nBI_nRBO
  _7_Segment_Display #(.active("false")) u_7_segment_display_1 (
    .g(1'b1), .f(1'b1), .a(1'b1), .b(j_k_ff_1_qn), .e(1'b1), .d(1'b1), .c(j_k_ff_1_qn), .dp(1'b1));
  LED #(.active("false")) PM (.in(j_k_ff_2_qn));
  Clock clock_1 (.out(clock_1_out));
  LED led_1 (.in(1'b1));
  _7_Segment_Display #(.active("false")) u_7_segment_display_2 (
    .g(n74ls247_2_g), .f(n74ls247_2_f), .a(n74ls247_2_a_2), .b(n74ls247_2_b_2), .e(n74ls247_2_e),
    .d(n74ls247_2_d_2), .c(n74ls247_2_c_2), .dp(1'b1));
  LED led_2 (.in(1'b1));
  _74LS90 u_74ls90_1 (
    .R9__1(1'b0), .R9__2(1'b0), .nCKA(clock_1_out), .nCKB(n74ls90_1_qa[0]), .R0__1(1'b0), .R0__2(1'b0),
    .QA(n74ls90_1_qa[0]), .QB(n74ls90_1_qa[1]), .QC(n74ls90_1_qa[2]), .QD(n74ls90_1_qa[3]), .VCC(1'b1),
    .GND(1'b0));  // open: NC, NC_2
  _7_Segment_Display #(.active("false")) u_7_segment_display_3 (
    .g(n74ls247_5_g), .f(n74ls247_5_f), .a(n74ls247_5_a_2), .b(n74ls247_5_b_2), .e(n74ls247_5_e),
    .d(n74ls247_5_d_2), .c(n74ls247_5_c_2), .dp(1'b1));
  _7_Segment_Display #(.active("false")) u_7_segment_display_4 (
    .g(n74ls247_1_g), .f(n74ls247_1_f), .a(n74ls247_1_a_2), .b(n74ls247_1_b_2), .e(n74ls247_1_e),
    .d(n74ls247_1_d_2), .c(n74ls247_1_c_2), .dp(1'b1));
  LED led_3 (.in(1'b1));
  _7_Segment_Display #(.active("false")) u_7_segment_display_5 (
    .g(n74ls247_4_g), .f(n74ls247_4_f), .a(n74ls247_4_a_2), .b(n74ls247_4_b_2), .e(n74ls247_4_e),
    .d(n74ls247_4_d_2), .c(n74ls247_4_c_2), .dp(1'b1));
  LED led_4 (.in(1'b1));
  _74LS90 u_74ls90_2 (
    .R9__1(1'b0), .R9__2(1'b0), .nCKA(n74ls90_1_qa[3]), .nCKB(n74ls90_2_qa[0]), .R0__1(n74ls90_2_qa[1]),
    .R0__2(n74ls90_2_qa[2]), .QA(n74ls90_2_qa[0]), .QB(n74ls90_2_qa[1]), .QC(n74ls90_2_qa[2]), .VCC(1'b1),
    .GND(1'b0));  // open: NC, NC_2, QD
  _7_Segment_Display #(.active("false")) u_7_segment_display_6 (
    .g(n74ls247_3_g), .f(n74ls247_3_f), .a(n74ls247_3_a_2), .b(n74ls247_3_b_2), .e(n74ls247_3_e),
    .d(n74ls247_3_d_2), .c(n74ls247_3_c_2), .dp(1'b1));
  Multiplexer #(.enable("false")) multiplexer_1 (
    .in0(n74ls90_2_qa[2]), .in1(clock_1_out), .out(multiplexer_1_out), .sel(Minutes));
  _74LS247 u_74ls247_3 (
    .A(n74ls90_1_qa[0]), .B(n74ls90_1_qa[1]), .C(n74ls90_1_qa[2]), .D(n74ls90_1_qa[3]), .nLT(1'b1),
    .nRBI(1'b1), .a_2(n74ls247_3_a_2), .b_2(n74ls247_3_b_2), .c_2(n74ls247_3_c_2), .d_2(n74ls247_3_d_2),
    .e(n74ls247_3_e), .f(n74ls247_3_f), .g(n74ls247_3_g), .VCC(1'b1), .GND(1'b0));  // open: nBI_nRBO
  _74LS90 u_74ls90_3 (
    .R9__1(1'b0), .R9__2(1'b0), .nCKA(multiplexer_1_out), .nCKB(n74ls90_3_qa[0]), .R0__1(1'b0), .R0__2(1'b0),
    .QA(n74ls90_3_qa[0]), .QB(n74ls90_3_qa[1]), .QC(n74ls90_3_qa[2]), .QD(n74ls90_3_qa[3]), .VCC(1'b1),
    .GND(1'b0));  // open: NC, NC_2
  _74LS90 u_74ls90_4 (
    .R9__1(1'b0), .R9__2(1'b0), .nCKA(n74ls90_3_qa[3]), .nCKB(n74ls90_4_qa[0]), .R0__1(n74ls90_4_qa[1]),
    .R0__2(n74ls90_4_qa[2]), .QA(n74ls90_4_qa[0]), .QB(n74ls90_4_qa[1]), .QC(n74ls90_4_qa[2]), .VCC(1'b1),
    .GND(1'b0));  // open: NC, NC_2, QD
  _74LS247 u_74ls247_4 (
    .A(n74ls90_2_qa[0]), .B(n74ls90_2_qa[1]), .C(n74ls90_2_qa[2]), .D(1'b0), .nLT(1'b1), .nRBI(1'b1),
    .a_2(n74ls247_4_a_2), .b_2(n74ls247_4_b_2), .c_2(n74ls247_4_c_2), .d_2(n74ls247_4_d_2), .e(n74ls247_4_e),
    .f(n74ls247_4_f), .g(n74ls247_4_g), .VCC(1'b1), .GND(1'b0));  // open: nBI_nRBO
  _74LS247 u_74ls247_5 (
    .A(n74ls90_3_qa[0]), .B(n74ls90_3_qa[1]), .C(n74ls90_3_qa[2]), .D(n74ls90_3_qa[3]), .nLT(1'b1),
    .nRBI(1'b1), .a_2(n74ls247_5_a_2), .b_2(n74ls247_5_b_2), .c_2(n74ls247_5_c_2), .d_2(n74ls247_5_d_2),
    .e(n74ls247_5_e), .f(n74ls247_5_f), .g(n74ls247_5_g), .VCC(1'b1), .GND(1'b0));  // open: nBI_nRBO
  Multiplexer #(.enable("false")) multiplexer_2 (
    .in0(n74ls90_4_qa[2]), .in1(clock_1_out), .out(multiplexer_2_out), .sel(Hours));
  _74LS163 u_74ls163_1 (
    .VCC(1'b1), .nLOAD(nand_3_out), .A(1'b1), .B(1'b0), .nCLK(nand_1_out), .C(1'b0), .D(1'b0),
    .nCLR(nand_2_out), .ENP(1'b1), .ENT(1'b1), .GND(1'b0), .QA(n74ls163_1_qa[0]), .QB(n74ls163_1_qa[1]),
    .QC(n74ls163_1_qa[2]), .QD(n74ls163_1_qa[3]));  // open: RCO
  nand nand_1 (nand_1_out, multiplexer_2_out, multiplexer_2_out);
  nand nand_2 (nand_2_out, n74ls163_1_qa[0], n74ls163_1_qa[3]);
  nand nand_3 (nand_3_out, n74ls163_1_qa[1], j_k_ff_1_q);
  nand nand_4 (nand_4_out, nand_2_out, nand_3_out);
  J_K_Flip_Flop #(.trigger("falling")) j_k_ff_1 (
    .J(1'b1), .clk(nand_4_out), .K(1'b1), .Q(j_k_ff_1_q), .Qn(j_k_ff_1_qn));  // open: preset, en, reset
  J_K_Flip_Flop #(.trigger("falling")) j_k_ff_2 (
    .J(1'b1), .clk(nand_3_out), .K(1'b1), .Qn(j_k_ff_2_qn));  // open: Q, preset, en, reset

  // Notes on the sheet:
  //   1 - 1Hz oscillator
  //   4 - decade counters (7490)
  //   1 - binary counter (74163)
  //   4 - 2-input NAND gates (7400)
  //   2 - negedge JK-flip-flops (7473)
  //   6/4 - 7-seg displays
  //   5/3 - LEDs
  //   2 - SPDT push buttons
  //   5/3 - BCD to 7-seg decoders (74247)
  //   feedback loop
endmodule

module _74LS247 (
  input  VCC,
  input  GND,
  input  A,
  input  B,
  input  C,
  input  D,
  input  nLT,
  input  nRBI,
  output a_2,
  output b_2,
  output c_2,
  output d_2,
  output e,
  output nBI_nRBO,
  output f,
  output g
);

  wire and_1_out, and_2_out, and_3_out, and_4_out, and_5_out, and_6_out, and_7_out, and_8_out, and_9_out,
       and_10_out, and_11_out, and_12_out, and_13_out, and_14_out, and_15_out, and_16_out, and_17_out,
       buffer_1_out, nand_1_out, nand_2_out, nand_3_out, nand_4_out, nand_5_out, nand_6_out, nand_7_out,
       nor_1_out, nor_2_out, nor_3_out, nor_4_out, nor_5_out, nor_6_out, nor_7_out, not_1_out, not_2_out,
       not_3_out, not_4_out, not_5_out, not_6_out;

  nand nand_1 (nand_1_out, A, not_2_out);
  nand nand_2 (nand_2_out, B, not_2_out);
  nand nand_3 (nand_3_out, C, not_2_out);
  not not_1 (not_1_out, D);
  not not_2 (not_2_out, not_3_out);
  not not_3 (not_3_out, nLT);
  not not_4 (not_4_out, nRBI);
  nand nand_4 (nand_4_out, nand_1_out, not_5_out);
  nand nand_5 (nand_5_out, nand_2_out, not_5_out);
  nand nand_6 (nand_6_out, nand_3_out, not_5_out);
  nand nand_7 (nand_7_out, not_1_out, not_5_out);
  not not_5 (not_5_out, not_6_out);
  not not_6 (not_6_out, nBI_nRBO);
  nand nand_8 (nBI_nRBO, not_2_out, not_4_out, not_1_out, nand_3_out, nand_2_out, nand_1_out);
  and and_1 (and_1_out, nand_5_out, nand_7_out);
  and and_2 (and_2_out, nand_1_out, nand_2_out, nand_6_out);
  and and_3 (and_3_out, nand_4_out, nand_2_out, nand_3_out, not_1_out);
  and and_4 (and_4_out, nand_5_out, nand_7_out);
  and and_5 (and_5_out, nand_4_out, nand_2_out, nand_6_out);
  and and_6 (and_6_out, nand_1_out, nand_5_out, nand_6_out);
  and and_7 (and_7_out, nand_6_out, nand_7_out);
  and and_8 (and_8_out, nand_1_out, nand_5_out, nand_3_out);
  and and_9 (and_9_out, nand_4_out, nand_2_out, nand_3_out, not_1_out);
  and and_10 (and_10_out, nand_1_out, nand_2_out, nand_6_out);
  and and_11 (and_11_out, nand_4_out, nand_5_out, nand_6_out);
  buf buffer_1 (buffer_1_out, nand_4_out);
  and and_12 (and_12_out, nand_2_out, nand_6_out);
  and and_13 (and_13_out, nand_4_out, nand_5_out);
  and and_14 (and_14_out, nand_5_out, nand_3_out);
  and and_15 (and_15_out, nand_4_out, nand_3_out, not_1_out);
  and and_16 (and_16_out, nand_4_out, nand_5_out, nand_6_out);
  and and_17 (and_17_out, nand_2_out, nand_3_out, not_1_out, not_2_out);
  nor nor_1 (nor_1_out, and_1_out, and_2_out, and_3_out);
  nor nor_2 (nor_2_out, and_4_out, and_5_out, and_6_out);
  nor nor_3 (nor_3_out, and_7_out, and_8_out);
  nor nor_4 (nor_4_out, and_9_out, and_10_out, and_11_out);
  nor nor_5 (nor_5_out, buffer_1_out, and_12_out);
  nor nor_6 (nor_6_out, and_13_out, and_14_out, and_15_out);
  nor nor_7 (nor_7_out, and_16_out, and_17_out);
  not not_7 (a_2, nor_1_out);
  not not_8 (b_2, nor_2_out);
  not not_9 (c_2, nor_3_out);
  not not_10 (d_2, nor_4_out);
  not not_11 (e, nor_5_out);
  not not_12 (f, nor_6_out);
  not not_13 (g, nor_7_out);

  // Notes on the sheet:
  //   = AB'C'D' + A'B'C + BD
  //   = AB'C + A'BC + BD
  //   = A'BC' + CD
  //   = AB'C'D' + ABC + A'B'C
  //   = A + B'C
  //   = AC'D' + AB + BC'
  //   = ABC + B'C'D'
endmodule

module _74LS90 (
  input  VCC,
  input  GND,
  input  R9__1,
  input  R9__2,
  input  nCKA,
  input  nCKB,
  input  R0__1,
  input  R0__2,
  output NC,
  output NC_2,
  output QA,
  output QB,
  output QC,
  output QD
);

  wire and_1_out, nand_1_out, nand_2_out, not_1_out, not_2_out, not_3_out, not_4_out, not_5_out, not_6_out,
       not_7_out, not_8_out, or_1_out, or_2_out, s_r_ff_1_qn;

  nand nand_1 (nand_1_out, R9__1, R9__2);
  nand nand_2 (nand_2_out, R0__1, R0__2);
  not not_1 (not_1_out, nCKA);
  not not_2 (not_2_out, nand_1_out);
  not not_3 (not_3_out, nCKB);
  not not_4 (not_4_out, QB);
  and and_1 (and_1_out, QC, QB);
  not not_5 (not_5_out, nCKB);
  not not_6 (not_6_out, nand_1_out);
  J_K_Flip_Flop j_k_ff_1 (
    .J(1'b1), .clk(not_1_out), .K(1'b1), .Q(QA), .preset(not_2_out), .reset(not_7_out));  // open: Qn, en
  not not_7 (not_7_out, nand_2_out);
  J_K_Flip_Flop j_k_ff_2 (
    .J(s_r_ff_1_qn), .clk(not_3_out), .K(1'b1), .Q(QB), .reset(or_1_out));  // open: Qn, preset, en
  or or_1 (or_1_out, ~nand_2_out, ~nand_1_out);  // OR_Gate
  J_K_Flip_Flop j_k_ff_3 (.J(1'b1), .clk(not_4_out), .K(1'b1), .Q(QC), .reset(or_2_out));  // open: Qn, preset, en
  or or_2 (or_2_out, ~nand_2_out, ~nand_1_out);  // OR_Gate
  S_R_Flip_Flop s_r_ff_1 (
    .S(and_1_out), .clk(not_5_out), .R(QD), .Q(QD), .Qn(s_r_ff_1_qn), .preset(not_6_out), .reset(not_8_out));  // open: en
  not not_8 (not_8_out, nand_2_out);
endmodule

module _74LS163 (
  input  VCC,
  input  GND,
  input  nLOAD,
  input  A,
  input  B,
  input  nCLK,
  input  C,
  input  D,
  input  nCLR,
  input  ENP,
  input  ENT,
  output QA,
  output QB,
  output QC,
  output QD,
  output RCO
);

  wire and_1_out, and_2_out, and_3_out, and_4_out, and_5_out, and_6_out, and_7_out, and_8_out, and_9_out,
       and_10_out, and_11_out, and_12_out, nand_1_out, nand_2_out, nand_3_out, nand_4_out, nand_5_out,
       nand_6_out, nand_7_out, nand_8_out, not_1_out, not_2_out, not_3_out, or_1_out, or_2_out, or_3_out,
       or_4_out, or_5_out;

  not not_1 (not_1_out, nCLR);
  not not_2 (not_2_out, not_1_out);
  and and_1 (and_1_out, ENP, ENT);
  or or_1 (or_1_out, ~nLOAD, ~not_2_out);  // OR_Gate
  and and_2 (and_2_out, QA, and_1_out);
  not not_3 (not_3_out, nCLK);
  and and_3 (and_3_out, QB, QA, and_1_out);
  and and_4 (and_4_out, QC, QB, QA, and_1_out);
  nand nand_1 (nand_1_out, or_1_out, nand_2_out);
  or or_2 (or_2_out, and_1_out, or_1_out);
  nand nand_2 (nand_2_out, A, not_2_out, or_1_out);
  nand nand_3 (nand_3_out, or_1_out, nand_4_out);
  or or_3 (or_3_out, and_2_out, or_1_out);
  nand nand_4 (nand_4_out, B, not_2_out, or_1_out);
  nand nand_5 (nand_5_out, or_1_out, nand_6_out);
  or or_4 (or_4_out, and_3_out, or_1_out);
  nand nand_6 (nand_6_out, C, not_2_out, or_1_out);
  nand nand_7 (nand_7_out, or_1_out, nand_8_out);
  or or_5 (or_5_out, and_4_out, or_1_out);
  nand nand_8 (nand_8_out, D, or_1_out, not_2_out);
  and and_5 (and_5_out, nand_1_out, or_2_out);
  and and_6 (and_6_out, or_2_out, nand_2_out);
  and and_7 (and_7_out, nand_3_out, or_3_out);
  and and_8 (and_8_out, or_3_out, nand_4_out);
  and and_9 (and_9_out, nand_5_out, or_4_out);
  and and_10 (and_10_out, or_4_out, nand_6_out);
  and and_11 (and_11_out, nand_7_out, or_5_out);
  and and_12 (and_12_out, or_5_out, nand_8_out);
  J_K_Flip_Flop #(.trigger("falling")) j_k_ff_1 (
    .J(and_5_out), .clk(not_3_out), .K(and_6_out), .Q(QA));  // open: Qn, preset, en, reset
  J_K_Flip_Flop #(.trigger("falling")) j_k_ff_2 (
    .J(and_7_out), .clk(not_3_out), .K(and_8_out), .Q(QB));  // open: Qn, preset, en, reset
  J_K_Flip_Flop #(.trigger("falling")) j_k_ff_3 (
    .J(and_9_out), .clk(not_3_out), .K(and_10_out), .Q(QC));  // open: Qn, preset, en, reset
  J_K_Flip_Flop #(.trigger("falling")) j_k_ff_4 (
    .J(and_11_out), .clk(not_3_out), .K(and_12_out), .Q(QD));  // open: Qn, preset, en, reset
  and and_13 (RCO, QD, QC, QB, QA, ENT);
endmodule
